// Digital circuit hardware.dig as structural Verilog
module hardware (
  input  clk,
  input  [15:0] in_2,
  input  in_3,
  input  [3:0] in_4,
  input  [3:0] in_5,
  input  [3:0] in_6,
  input  [3:0] in_7,
  input  [15:0] in_8,
  input  [15:0] in_9
);

  wire alu_1_fn;
  wire [15:0] registerfile_1_da, registerfile_1_db;

  RegisterFile #(.AddrBits(4), .Bits(16)) registerfile_1 (
    .Din(in_2), .we(in_3), .Rw(in_4), .C(clk), .Ra(in_5), .Rb(in_6), .Da(registerfile_1_da),
    .Db(registerfile_1_db));
  // Probe on registerfile_1_da
  // Probe on registerfile_1_db
  alu alu_1 (.Op(in_7), .TData(in_8), .AData(in_9), .fN(alu_1_fn));  // open: RData, fZ
  // Probe on alu_1_fn
endmodule
